// Logisim project control_logic.circ as structural Verilog: 1 circuit, main circuit control_logic
module control_logic (
  input  [31:0] inst,
  input  BrEq,
  input  BrLt,
  output PCSel,
  output RegWEn,
  output [2:0] ImmSel,
  output BrUn,
  output ASel,
  output BSel,
  output [3:0] ALUSel,
  output MemRW,
  output [1:0] WBSel,
  output CSRSel,
  output CSRWen
);

  wire beq_out, bge_out, bgeu_out, blt_out, bltu_out, bne_out, comparator_6_eq, comparator_7_eq,
       comparator_15_eq, comparator_16_eq, comparator_17_eq, comparator_18_eq, comparator_19_eq,
       comparator_20_eq, comparator_21_eq, comparator_22_eq, comparator_23_eq, comparator_24_eq,
       comparator_25_eq, comparator_26_eq, comparator_27_eq, comparator_28_eq, comparator_29_eq,
       comparator_30_eq, comparator_31_eq, comparator_32_eq, comparator_33_eq, is_auipc, is_branch, is_I,
       is_jal, is_jalr, is_load, is_lui, is_mul, is_mulh, is_R, is_SB, is_sra_or_srai, is_sub, is_U, is_UJ,
       not_1_out, not_2_out, not_3_out, or_2_out, or_4_out, or_7_out, or_8_out, or_9_out, or_10_out,
       or_12_out;
  wire [1:0] multiplexer_12_out, multiplexer_13_out;
  wire [2:0] multiplexer_3_out, multiplexer_5_out, multiplexer_8_out, multiplexer_9_out;
  wire [3:0] multiplexer_1_out, multiplexer_2_out, multiplexer_4_out, multiplexer_6_out, multiplexer_7_out;

  Comparator #(.width(7)) comparator_1 (.a(inst[6:0]), .b(7'b0110011), .eq(is_R));  // open: gt, lt
  Comparator #(.width(7)) comparator_2 (.a(inst[6:0]), .b(7'b0000011), .eq(is_load));  // open: gt, lt
  Comparator #(.width(7)) comparator_3 (.a(inst[6:0]), .b(7'b0010011), .eq(is_I));  // open: gt, lt
  Comparator #(.width(7)) comparator_4 (.a(inst[6:0]), .b(7'b0100011), .eq(MemRW));  // open: gt, lt
  Comparator #(.width(7)) comparator_5 (.a(inst[6:0]), .b(7'b1100011), .eq(is_SB));  // open: gt, lt
  Comparator #(.width(7)) comparator_6 (.a(inst[6:0]), .b(7'b0010111), .eq(comparator_6_eq));  // open: gt, lt
  or or_1 (is_U, comparator_6_eq, comparator_7_eq);
  Comparator #(.width(7)) comparator_7 (.a(inst[6:0]), .b(7'b0110111), .eq(comparator_7_eq));  // open: gt, lt
  Comparator #(.width(7)) comparator_8 (.a(inst[6:0]), .b(7'b1101111), .eq(is_UJ));  // open: gt, lt
  Comparator #(.width(7)) comparator_9 (.a(inst[6:0]), .b(7'b1100111), .eq(is_jalr));  // open: gt, lt
  Comparator #(.width(7)) comparator_10 (.a(inst[6:0]), .b(7'b1110011), .eq(CSRWen));  // open: gt, lt
  Comparator #(.width(7)) comparator_11 (.a(inst[6:0]), .b(7'b1100011), .eq(is_branch));  // open: gt, lt
  Comparator #(.width(7)) comparator_12 (.a(inst[6:0]), .b(7'b0010111), .eq(is_auipc));  // open: gt, lt
  Comparator #(.width(7)) comparator_13 (.a(inst[6:0]), .b(7'b0110111), .eq(is_lui));  // open: gt, lt
  Comparator #(.width(7)) comparator_14 (.a(inst[6:0]), .b(7'b1101111), .eq(is_jal));  // open: gt, lt
  Comparator #(.width(3)) comparator_15 (.a(inst[14:12]), .b(3'b000), .eq(comparator_15_eq));  // open: gt, lt
  and and_1 (is_mul, comparator_15_eq, is_R, comparator_16_eq);
  Comparator #(.width(7)) comparator_16 (.a(inst[31:25]), .b(7'b0000001), .eq(comparator_16_eq));  // open: gt, lt
  Comparator #(.width(3)) comparator_17 (.a(inst[14:12]), .b(3'b000), .eq(comparator_17_eq));  // open: gt, lt
  and and_2 (is_sub, comparator_17_eq, is_R, comparator_18_eq);
  Comparator #(.width(7)) comparator_18 (.a(inst[31:25]), .b(7'b0100000), .eq(comparator_18_eq));  // open: gt, lt
  Comparator #(.width(3)) comparator_19 (.a(inst[14:12]), .b(3'b001), .eq(comparator_19_eq));  // open: gt, lt
  and and_3 (is_mulh, comparator_19_eq, is_R, comparator_20_eq);
  Comparator #(.width(7)) comparator_20 (.a(inst[31:25]), .b(7'b0000001), .eq(comparator_20_eq));  // open: gt, lt
  Comparator #(.width(3)) comparator_21 (.a(inst[14:12]), .b(3'b101), .eq(comparator_21_eq));  // open: gt, lt
  Comparator #(.width(7)) comparator_22 (.a(inst[31:25]), .b(7'b0100000), .eq(comparator_22_eq));  // open: gt, lt
  or or_2 (or_2_out, is_R, is_I);
  and and_4 (is_sra_or_srai, comparator_21_eq, comparator_22_eq, or_2_out);
  Multiplexer #(.enable("false"), .select(3), .width(4)) multiplexer_1 (
    .in0(4'b0000), .in1(4'b0110), .in2(4'b0111), .in3(4'b1011), .in4(4'b0011), .in5(4'b0100), .in6(4'b0010),
    .in7(4'b0001), .out(multiplexer_1_out), .sel(inst[14:12]));
  Multiplexer #(.enable("false"), .width(4)) multiplexer_2 (
    .in0(multiplexer_1_out), .in1(4'b1010), .out(multiplexer_2_out), .sel(is_mul));
  or or_3 (RegWEn, is_R, is_I, is_load, is_auipc, is_lui, is_jal, is_jalr);
  Multiplexer #(.enable("false"), .width(3)) multiplexer_3 (
    .in0(3'b000), .in1(3'b001), .out(multiplexer_3_out), .sel(MemRW));
  Multiplexer #(.enable("false"), .width(4)) multiplexer_4 (
    .in0(multiplexer_2_out), .in1(4'b1100), .out(multiplexer_4_out), .sel(is_sub));
  Multiplexer #(.enable("false"), .width(3)) multiplexer_5 (
    .in0(multiplexer_3_out), .in1(3'b010), .out(multiplexer_5_out), .sel(is_SB));
  Multiplexer #(.enable("false"), .width(4)) multiplexer_6 (
    .in0(multiplexer_4_out), .in1(4'b1110), .out(multiplexer_6_out), .sel(is_mulh));
  Multiplexer #(.enable("false"), .width(4)) multiplexer_7 (
    .in0(multiplexer_6_out), .in1(4'b0101), .out(multiplexer_7_out), .sel(is_sra_or_srai));
  Multiplexer #(.enable("false"), .width(3)) multiplexer_8 (
    .in0(multiplexer_5_out), .in1(3'b011), .out(multiplexer_8_out), .sel(is_U));
  Multiplexer #(.enable("false"), .width(3)) multiplexer_9 (
    .in0(multiplexer_8_out), .in1(3'b100), .out(multiplexer_9_out), .sel(is_UJ));
  or or_4 (or_4_out, comparator_23_eq, comparator_24_eq);
  Comparator #(.width(7)) comparator_23 (.a(inst[6:0]), .b(7'b0110011), .eq(comparator_23_eq));  // open: gt, lt
  Comparator #(.width(7)) comparator_24 (.a(inst[6:0]), .b(7'b0010011), .eq(comparator_24_eq));  // open: gt, lt
  Multiplexer #(.enable("false"), .width(3)) multiplexer_10 (
    .in0(multiplexer_9_out), .in1(3'b101), .out(ImmSel), .sel(CSRWen));
  and and_5 (CSRSel, CSRWen, comparator_25_eq);
  Comparator #(.width(3)) comparator_25 (.a(inst[14:12]), .b(3'b101), .eq(comparator_25_eq));  // open: gt, lt
  Multiplexer #(.enable("false"), .width(4)) multiplexer_11 (
    .in0(4'b0000), .in1(multiplexer_7_out), .out(ALUSel), .sel(or_4_out));
  or or_5 (ASel, is_jal, is_auipc, is_SB);
  or or_6 (BSel, is_I, is_load, is_SB, is_jalr, is_auipc, is_lui, is_jal);
  Multiplexer #(.enable("false"), .width(2)) multiplexer_12 (
    .in0(2'b00), .in1(2'b01), .out(multiplexer_12_out), .sel(or_7_out));
  or or_7 (or_7_out, is_R, is_auipc, is_I);
  Comparator #(.width(3)) comparator_26 (.a(inst[14:12]), .b(3'b000), .eq(comparator_26_eq));  // open: gt, lt
  Comparator #(.width(3)) comparator_27 (.a(inst[14:12]), .b(3'b001), .eq(comparator_27_eq));  // open: gt, lt
  Comparator #(.width(3)) comparator_28 (.a(inst[14:12]), .b(3'b100), .eq(comparator_28_eq));  // open: gt, lt
  Comparator #(.width(3)) comparator_29 (.a(inst[14:12]), .b(3'b101), .eq(comparator_29_eq));  // open: gt, lt
  Comparator #(.width(3)) comparator_30 (.a(inst[14:12]), .b(3'b110), .eq(comparator_30_eq));  // open: gt, lt
  Comparator #(.width(3)) comparator_31 (.a(inst[14:12]), .b(3'b111), .eq(comparator_31_eq));  // open: gt, lt
  Multiplexer #(.enable("false"), .width(2)) multiplexer_13 (
    .in0(multiplexer_12_out), .in1(2'b10), .out(multiplexer_13_out), .sel(or_8_out));
  or or_8 (or_8_out, is_jalr, is_jal);
  and beq (beq_out, comparator_26_eq, BrEq, is_branch);
  not not_1 (not_1_out, BrEq);
  and bne (bne_out, comparator_27_eq, not_1_out, is_branch);
  and blt (blt_out, comparator_28_eq, BrLt, is_branch);
  not not_2 (not_2_out, BrLt);
  and bge (bge_out, comparator_29_eq, not_2_out, is_branch);
  and bltu (bltu_out, comparator_30_eq, BrLt, is_branch);
  not not_3 (not_3_out, BrLt);
  and bgeu (bgeu_out, comparator_31_eq, not_3_out, is_branch);
  Multiplexer #(.enable("false"), .width(2)) multiplexer_14 (
    .in0(multiplexer_13_out), .in1(2'b11), .out(WBSel), .sel(is_lui));
  Comparator #(.width(3)) comparator_32 (.a(inst[14:12]), .b(3'b111), .eq(comparator_32_eq));  // open: gt, lt
  Comparator #(.width(3)) comparator_33 (.a(inst[14:12]), .b(3'b110), .eq(comparator_33_eq));  // open: gt, lt
  or or_9 (or_9_out, comparator_32_eq, comparator_33_eq);
  or or_10 (or_10_out, beq_out, bne_out, blt_out, bge_out, bltu_out, bgeu_out);
  and and_6 (BrUn, or_9_out, is_branch);
  or or_11 (PCSel, or_10_out, or_12_out);
  or or_12 (or_12_out, is_jal, is_jalr);

  // Other names for the same wires on the sheet: opcode[6:0] = inst[6:0]; rd[4:0] = inst[11:7];
  //   funct3[2:0] = inst[14:12]; rs1[4:0] = inst[19:15]; rs2[4:0] = inst[24:20]; funct7[6:0] = inst[31:25];
  //   is_csrw_or_csrwi = CSRWen; is_S = MemRW

  // Notes on the sheet:
  //   INPUTS to your circuit
  //   is_what
  //   DON'T CHANGE THE LOCATIONS OF THE INPUTS AND OUTPUTS!
  //   OUTPUT from your circuit
  //   RegWEn
  //   ALUSel
  //   ImmSel
  //   0->I, 1->S, 2->SB, 3->U, 4->UJ, 5->csrwi
  //   CSRSel and CSRWen
  //   ASel and BSel
  //   WBSel
  //   0->load, 1->ALUout, 2->PC4, 3->only_Imm
  //   PCSel and BrUn
  //   sighed or unsigned
  //   MemRW
endmodule
